// Digital circuit ProjetoMicroarquitetural.dig as structural Verilog
module ProjetoMicroarquitetural (
  input  clk
);

  wire ERRO, IMM, LD, MWRITE, STR;
  wire [1:0] DADO, PC, TPIMM;
  wire [2:0] F3, ULA;
  wire [4:0] RD, RS1, RS2;
  wire [6:0] F7, OPCODE;
  wire [31:0] add_1_s, add_2_s, brg_1_s1, brg_1_s2, MDD_d, multiplexer_1_out, multiplexer_2_out, SDADO, SIMM,
       SPC, SULA;

  REG u_PC (.CLK(clk), .E(add_1_s), .S(SPC));
  ADD add_1 (.RS1(multiplexer_1_out), .RS2(SPC), .Cout(ERRO), .S(add_1_s));
  ROM #(.AddrBits(4), .isProgramMemory("true"), .Bits(32)) MI (
    .A(SPC[3:0]), .sel(1'b1), .D({F7, RS2, RS1, F3, RD, OPCODE}));
  LED led_1 (.in(ERRO));
  Multiplexer #(.Selector_Bits(2), .Bits(32)) multiplexer_1 (
    .sel(PC), .in_0({32{1'b0}}), .in_1(32'h4), .in_2(SULA), .in_3(SIMM), .out(multiplexer_1_out));
  CC cc_1 (
    .OPCD(OPCODE), .F3(F3), .F7(F7), .DADO(DADO), .PC(PC), .LD(LD), .STR(STR), .BRG(MWRITE), .TPIMM(TPIMM),
    .IMM(IMM), .SULA(SULA), .ULA(ULA));
  BRG brg_1 (.RS1(RS1), .RS2(RS2), .RD(RD), .MWRITE(MWRITE), .CLK(clk), .DADO(SDADO), .S1(brg_1_s1), .S2(brg_1_s2));
  // IMMEXT immext_1: pin names not known; wires that end beside it: {F7, RS2, RS1, F3, RD}, TPIMM, SIMM
  Multiplexer #(.Bits(32)) multiplexer_2 (.sel(IMM), .in_0(brg_1_s2), .in_1(SIMM), .out(multiplexer_2_out));
  ULA ula_1 (.RS1(brg_1_s1), .RS2(multiplexer_2_out), .E(ULA), .ERRO(ERRO), .S(SULA));
  RAMDualPort #(.AddrBits(5), .Bits(32)) MDD (.A(SULA[4:0]), .Din(SULA), .str(STR), .C(clk), .ld(LD), .D(MDD_d));
  Multiplexer #(.Selector_Bits(2), .Bits(32)) multiplexer_3 (
    .sel(DADO), .in_0({32{1'b0}}), .in_1(add_2_s), .in_2(MDD_d), .in_3(SULA), .out(SDADO));
  ADD add_2 (.RS1(32'h4), .RS2(SPC), .Cout(ERRO), .S(add_2_s));
endmodule
